# Fritzing sketch wiring (saved by Fritzing 0.9.8b)

parts:
  A1 = Werner Rothschopf (modified to ESP32-S3-DevKitC dual USB by vanepp Aug 2024)
  Part1 = InvenSense MPU6050
  U1 = Mini-360 DC-DC Buck converter [package=THT]
  S1 = Toggle Switch [package=THT]
  Mod1 = 3S-BMS
  Mod2 = Passive Buzzer
  J1 = female pin header, 8 pins [form="♀ (female)"]
  J2 = female pin header, 8 pins [form="♀ (female)"]
  Part4 = Lithium Ion Polymer Battery 3.7v 2000mAh [part_number=2011]
  Part3 = Lithium Ion Polymer Battery 3.7v 2000mAh [part_number=2011]
  Part2 = Lithium Ion Polymer Battery 3.7v 2000mAh [part_number=2011]
  J3 = female pin header, 11 pins [form="♀ (female)"]

nets:
  N1: A1.Pin_1, J1.pin6, J2.pin6, J3.pin1
  N2: A1.Pin_4, J3.pin6
  N3: A1.Pin_5, J3.pin5
  N4: A1.Pin_6, J3.pin4
  N5: A1.Pin_7, J3.pin3
  N6: A1.Pin_8, J1.pin8
  N7: A1.Pin_9, J1.pin7
  N8: A1.Pin_10, J1.pin5
  N9: A1.Pin_11, J1.pin4
  N10: A1.Pin_12, J3.pin2
  N11: A1.Pin_13, J3.pin7
  N12: A1.Pin_15, Part1.SCL
  N13: A1.Pin_16, J2.pin4
  N14: A1.Pin_17, J2.pin5
  N15: A1.Pin_18, J2.pin8
  N16: A1.Pin_19, J2.pin7
  N17: A1.Pin_20, A1.Pin_27, Mod2.S
  N18: A1.Pin_21, Part1.VCC, U1.OUT+
  N19: A1.Pin_22, A1.Pin_24, A1.Pin_29, A1.Pin_44, Part1.GND, U1.OUT-, Mod2.-, J3.pin11
  N20: A1.Pin_32, Part1.SDA
  N21: A1.Pin_33, J1.pin3
  N22: A1.Pin_40, J3.pin8
  N23: A1.Pin_41, J3.pin9
  N24: U1.IN-, Mod1.-, J1.pin2, J2.pin2
  N25: U1.IN+, S1.L2, J1.pin1, J2.pin1
  N26: S1.COM, Mod1.+
  N27: Mod1.0V, Part2.negative
  N28: Mod1.4.2V, Part3.negative, Part2.positive
  N29: Mod1.8.4V, Part4.negative, Part3.positive
  N30: Mod1.12.6V, Part4.positive

notes:
  Mikrokontroler
  Penurun Tegangan
  Baterai
  Sistem Manajemen Baterai
  Sakelar
  Motor
  Sensor Garis
  Sensor Inersia
  Buzzer

custom parts:
  Werner Rothschopf (modified to ESP32-S3-DevKitC dual USB by vanepp Aug 2024): ESP32-S3 ESP32-S3-DevKitC-1 Dual USB development board Pyboard CircuitPython Micropython wifi BLE5.0 ESP32-S3.
  Mini-360 DC-DC Buck converter: Mini-360 DC-DC Buck converter. Tiny buck step down voltage converter, input voltage 4.75 to 23V output 1 to 17V adjustable. Available from ebay and the like.
  3S-BMS: 3S-BMS LIPO battery charger / protection unit. Note pcb does not match the board as it will likely connect with wires, so pcb is 6 pads suitable for .1in header pins.
  Lithium Ion Polymer Battery 3.7v 2000mAh: Lithium ion polymer (also known as 'lipo' or 'lipoly') batteries are thin, light and powerful. The output ranges from 4.2V when completely charged to 3.7V. This battery has a capacity of 2000mAh. The batteries come pre-attached with a genuine 2-pin JST-PH connector as shown and include the necessary protection circuitry.
